# Fritzing sketch ESP8266 to FTDI (saved by Fritzing 0.9.2b)
breadboards: 1

parts:
  Part1 = FTDI Basic Programmer
  U3 = ESP8266 WiFi Module [part_number=ESP8266]

nets:
  N1: Part1.RXI, U3.VCC, U3.RST, U3.CH_PD, U3.TXD
  N2: Part1.TXO, U3.RXD
  N3: U3.GPIO_0, U3.GPIO_2, U3.GND

notes:
  Only connect purple to program the chip
  FTDI or PL2303
  WARNING:
  ONLY use 3.3 V

custom parts:
  ESP8266 WiFi Module: Generic WiFi Module based on the ESP8266 with onboard PCB antenna and UART communications
